# Fritzing sketch Schaltung (saved by Fritzing 0.8.0b)
breadboards: 1

parts:
  Anschluss_an_LED-streifen = RGB LED (com. anode, rbg) [package="5 mm [THT]"]
  Arduino_Uno = Arduino Uno (Rev3)
  Power_plug1 = Power plug
  Q1 = NPN-Transistor [package="TO92 [THT]"]
  Q2 = NPN-Transistor [package="TO92 [THT]"]
  Q3 = NPN-Transistor [package="TO92 [THT]"]

nets:
  VIN: Anschluss_an_LED-streifen.red_cathode, Arduino_Uno.VIN, Power_plug1.VCC
  N1: Anschluss_an_LED-streifen.common_anode, Q3.C
  N2: Anschluss_an_LED-streifen.blue_cathode, Q2.C
  N3: Anschluss_an_LED-streifen.green_cathode, Q1.C
  GND: Arduino_Uno.GND, Power_plug1.GND, Q1.E, Q2.E, Q3.E
  N4: Arduino_Uno.D9_PWM, Q1.B
  N5: Arduino_Uno.D10_PWM/SS, Q2.B
  N6: Arduino_Uno.D11_PWM/MOSI, Q3.B

notes:
  Wenn der Arduino High ausgibt ist die LED an wenn er low ausgibt ist sie aus.
  weißer Draht: nur nötig wenn der Arduino über keine eigene Stromversorgung verfügt.
  RGB-LED stellt LED-Streifen da.
  Steuerung für LED-Strifen
